// Logisim project CPU.circ as structural Verilog: 1 circuit, main circuit CPU
module CPU (
  output [15:0] out_1,
  output [23:0] out_2,
  output [15:0] out_3,
  output [15:0] out_4,
  output [15:0] out_5
);

  wire and_1_out, and_2_out, and_3_out, and_4_out, and_5_out, and_6_out, and_7_out, and_8_out, and_9_out,
       and_10_out, bitselector_1_out, clock_1_out, decoder_1_out0, decoder_1_out1, decoder_1_out2,
       decoder_1_out3, decoder_1_out4, decoder_1_out5, decoder_1_out6, decoder_1_out7, main_1_p7, not_1_out,
       not_2_out, not_3_out, or_1_out, or_2_out, or_3_out, or_4_out, or_5_out;
  wire [3:0] multiplexer_3_out;
  wire [6:0] bit_extender_3_out, main_1_p8;
  wire [7:0] multiplexer_4_out;
  wire [15:0] alu_1_out, main_1_p9, multiplexer_5_out, multiplexer_6_out, multiplexer_7_out,
       multiplexer_8_out, multiplexer_9_out, ram_2_data;
  wire [23:0] adder_1_out, adder_2_out, bit_extender_1_out, bit_extender_2_out, counter_1_q,
       multiplexer_1_out, multiplexer_2_out, ram_1_data, register_1_q;
  wire [31:0] register_2_q, register_3_q;

  Counter #(.width(24), .max('hffffff)) counter_1 (
    .load(and_2_out), .count(or_1_out), .Q(counter_1_q), .clk(clock_1_out));  // open: D, carry, clr
  or or_1 (or_1_out, and_2_out, and_3_out);
  not not_1 (not_1_out, and_2_out);
  Multiplexer #(.width(24), .enable("false")) multiplexer_1 (
    .in0(adder_2_out), .in1({out_1[11:4], out_2[15:0]}), .out(multiplexer_1_out), .sel(or_2_out));
  or or_2 (or_2_out, decoder_1_out3, and_1_out);
  assign bit_extender_1_out = {{23{1'b0}}, 1'b1};  // Bit_Extender bit_extender_1
  assign bit_extender_2_out = {{23{1'b0}}, 1'b1};  // Bit_Extender bit_extender_2
  Register #(.width(24), .trigger("falling")) register_1 (
    .D(multiplexer_2_out), .Q(register_1_q), .clk(clock_1_out));  // open: en, clr
  Multiplexer #(.width(24), .enable("false")) multiplexer_2 (
    .in0(ram_1_data), .in1(multiplexer_1_out), .out(multiplexer_2_out), .sel(not_1_out));
  Adder #(.width(24)) adder_1 (.a(adder_2_out), .b(bit_extender_1_out), .out(adder_1_out));  // open: cin, cout
  Adder #(.width(24)) adder_2 (.a(register_1_q), .b(bit_extender_2_out), .out(adder_2_out));  // open: cin, cout
  and and_1 (and_1_out, decoder_1_out6, bitselector_1_out);
  BitSelector #(.width(16)) bitselector_1 (.in(out_3), .out(bitselector_1_out), .sel(4'b0000));
  ROM #(.addrWidth(24), .dataWidth(32)) rom_1 (.addr(register_1_q), .data({out_2[15:0], out_1}));  // open: sel
  RAM #(.addrWidth(24), .dataWidth(24), .bus("separate")) ram_1 (
    .addr(counter_1_q), .din(adder_1_out), .data(ram_1_data), .str(and_3_out), .sel(or_1_out),
    .clk(clock_1_out), .ld(and_2_out));  // open: clr
  Decoder #(.select(4), .enable("false")) decoder_1 (
    .out0(decoder_1_out0), .out1(decoder_1_out1), .out2(decoder_1_out2), .out3(decoder_1_out3),
    .out4(decoder_1_out4), .out5(decoder_1_out5), .out6(decoder_1_out6), .out7(decoder_1_out7),
    .sel(out_1[3:0]));  // open: out8, out9, out10, out11, out12, out13, out14, out15
  Multiplexer #(.width(4), .enable("false")) multiplexer_3 (
    .in0(4'b0000), .in1(out_2[3:0]), .out(multiplexer_3_out), .sel(decoder_1_out1));
  and and_2 (and_2_out, out_1[5], decoder_1_out7);
  and and_3 (and_3_out, out_1[4], decoder_1_out7);
  not not_2 (not_2_out, out_1[4]);
  and and_4 (and_4_out, decoder_1_out1, not_2_out);
  or or_3 (or_3_out, and_4_out, decoder_1_out2, decoder_1_out0, and_10_out);
  and and_5 (and_5_out, decoder_1_out1, not_3_out);
  not not_3 (not_3_out, out_1[5]);
  Clock clock_1 (.out(clock_1_out));
  ALU alu_1 (.A(out_5), .B(out_3), .INSTR(out_1[7:4]), .Enable(decoder_1_out2), .OUT(alu_1_out));
  or or_4 (or_4_out, decoder_1_out2, decoder_1_out4, and_5_out, and_7_out);
  and and_6 (and_6_out, decoder_1_out1, out_1[5]);
  and and_7 (and_7_out, out_1[6], and_8_out);
  Multiplexer #(.width(8), .enable("false")) multiplexer_4 (
    .in0({8{1'b0}}), .in1(out_2[15:8]), .out(multiplexer_4_out), .sel(decoder_1_out1));
  Multiplexer #(.width(16), .enable("false")) multiplexer_5 (
    .in0(out_5), .in1(alu_1_out), .out(multiplexer_5_out), .sel(decoder_1_out2));
  or or_5 (or_5_out, and_6_out, and_10_out);
  and and_8 (and_8_out, decoder_1_out1, out_1[4]);
  and and_9 (and_9_out, out_1[5], decoder_1_out1);
  Multiplexer #(.width(16), .enable("false")) multiplexer_6 (
    .in0({16{1'b0}}), .in1(main_1_p9), .out(multiplexer_6_out), .sel(or_4_out));
  Multiplexer #(.width(16), .enable("false")) multiplexer_7 (
    .in0({16{1'b0}}), .in1(ram_2_data), .out(multiplexer_7_out), .sel(or_5_out));
  and and_10 (and_10_out, out_1[6], and_9_out);
  Multiplexer #(.width(16), .enable("false")) multiplexer_8 (
    .in0({out_1[15:8], multiplexer_4_out}), .in1(out_3), .out(multiplexer_8_out), .sel(out_1[6]));
  // REGARRAY_main main_1: pin names not known; wires that end beside it: multiplexer_5_out, out_2[7:4], out_1[15:12], multiplexer_3_out, or_3_out, clock_1_out, main_1_p7, main_1_p8, main_1_p9, out_3
  Multiplexer #(.width(16), .enable("false")) multiplexer_9 (
    .in0({16{1'b0}}), .in1(out_2[15:0]), .out(multiplexer_9_out), .sel(decoder_1_out0));
  assign out_5 = multiplexer_9_out | multiplexer_6_out | multiplexer_7_out;  // OR_Gate or_6, 16 bits wide
  Keyboard #(.trigger("falling")) keyboard_1 (.clk(clock_1_out), .re(main_1_p7), .data(main_1_p8));  // open: clr, avail
  Register #(.width(32)) register_2 (.Q(register_2_q), .clk(clock_1_out));  // open: D, en, clr
  Register #(.width(32)) register_3 (.Q(register_3_q), .clk(clock_1_out));  // open: D, en, clr
  RAM #(.addrWidth(16), .dataWidth(16), .bus("separate")) ram_2 (
    .addr(multiplexer_8_out), .din(out_5), .data(ram_2_data), .str(and_8_out), .sel(1'b1), .clk(clock_1_out),
    .ld(and_9_out));  // open: clr
  Bit_Extender #(.out_width(7)) bit_extender_3 (.in(out_5[7:0]), .out(bit_extender_3_out));
  DotMatrix #(.matrixcols(8), .matrixrows(8)) dotmatrix_1 (
    .col0(register_2_q[31:24]), .col1(register_2_q[23:16]), .col2(register_2_q[15:8]),
    .col3(register_2_q[7:0]), .col4(register_3_q[31:24]), .col5(register_3_q[23:16]),
    .col6(register_3_q[15:8]), .col7(register_3_q[7:0]));
  TTY #(.rows(32), .cols(100)) tty_1 (
    .data(bit_extender_3_out), .clk(clock_1_out), .we(decoder_1_out4), .clr(decoder_1_out5));

  assign out_2[23:16] = out_1[11:4];
  assign out_4 = out_2[15:0];

  // Notes on the sheet:
  //   0=immediate
  //   1=mov
  //   2=calc
  //   3=jmp
  //   4=wrt
  //   5=rssc
  //   6=JMI
  //   7=return/call
  //   contents of rom_1 (hex, n*v repeats v):
  //   300003 2010021 40006 27 27 27 0 20001 410001 102052 60006 100004 a0000 4 1100011 1010021 390000
  //   20001 102062 2000011 1010021 300000 20001 102042 11 10021 2020021 102092 2000011 17 10003 3010021
  //   a0000 20001 102022 3000011 1010021 300000 20001 102012 1000011 3010021 1020021 102002 3000011 17
  //   60003 27 17 60003 3000021 4
  //   Read
  //   Write
endmodule
