// Logisim project REGARRAY.circ as structural Verilog: 1 circuit, main circuit main
module main (
  input  [15:0] Data,
  input  [3:0] Read1,
  input  [3:0] Read0,
  input  [3:0] Write0,
  input  WritePerm,
  input  Clock,
  output [15:0] out_7,
  output [15:0] out_8
);

  wire and_1_out, and_2_out, and_3_out, and_4_out, decoder_1_out0, decoder_1_out1, decoder_1_out2,
       decoder_1_out3, keyboard_1_avail;
  wire [6:0] keyboard_1_data;
  wire [7:0] random_1_out;
  wire [15:0] bit_extender_1_out, bit_extender_2_out, register_1_q, register_2_q, register_3_q, register_4_q,
       register_5_q, register_6_q;

  Decoder #(.select(4), .enable("false")) decoder_1 (
    .out0(decoder_1_out0), .out1(decoder_1_out1), .out2(decoder_1_out2), .out3(decoder_1_out3), .sel(Write0));  // open: out4, out5, out6, out7, out8, out9, out10, out11, out12, out13, out14, out15
  Keyboard keyboard_1 (.clk(Clock), .re(Clock), .avail(keyboard_1_avail), .data(keyboard_1_data));  // open: clr
  and and_1 (and_1_out, WritePerm, decoder_1_out0);
  and and_2 (and_2_out, WritePerm, decoder_1_out1);
  and and_3 (and_3_out, WritePerm, decoder_1_out2);
  and and_4 (and_4_out, WritePerm, decoder_1_out3);
  assign bit_extender_1_out = {{9{1'b0}}, keyboard_1_data};  // Bit_Extender bit_extender_1
  assign bit_extender_2_out = {{8{1'b0}}, random_1_out};  // Bit_Extender bit_extender_2
  Random random_1 (.clk(Clock), .next(1'b1), .out(random_1_out));  // open: clr
  Register #(.width(16)) register_1 (.D(Data), .en(and_1_out), .Q(register_1_q), .clk(Clock));  // open: clr
  Register #(.width(16)) register_2 (.D(Data), .en(and_2_out), .Q(register_2_q), .clk(Clock));  // open: clr
  Register #(.width(16)) register_3 (.D(Data), .en(and_3_out), .Q(register_3_q), .clk(Clock));  // open: clr
  Register #(.width(16)) register_4 (.D(Data), .en(and_4_out), .Q(register_4_q), .clk(Clock));  // open: clr
  Register #(.width(16)) register_5 (
    .D(bit_extender_1_out), .en(keyboard_1_avail), .Q(register_5_q), .clk(Clock));  // open: clr
  Register #(.width(16)) register_6 (.D(bit_extender_2_out), .en(1'b1), .Q(register_6_q), .clk(Clock));  // open: clr
  Multiplexer #(.select(4), .width(16), .enable("false")) multiplexer_1 (
    .in0(register_1_q), .in1(register_2_q), .in2(register_3_q), .in3(register_4_q), .in4(register_5_q),
    .in5(register_6_q), .out(out_7), .sel(Read0));  // open: in6, in7, in8, in9, in10, in11, in12, in13, in14, in15
  Multiplexer #(.select(4), .width(16), .enable("false")) multiplexer_2 (
    .in0(register_1_q), .in1(register_2_q), .in2(register_3_q), .in3(register_4_q), .in4(register_5_q),
    .in5(register_6_q), .out(out_8), .sel(Read1));  // open: in6, in7, in8, in9, in10, in11, in12, in13, in14, in15
endmodule
